// Logisim project CPU.circ as structural Verilog
module ALU (
  input  [1:0] in_1,
  input  in_2,
  input  in_3,
  input  in_4,
  input  in_5,
  input  [1:0] in_6,
  input  in_7,
  input  in_8,
  input  in_9,
  input  in_10,
  output Overflow,
  output Overflow_2
);

  wire add_1_out_10, add_1_out_11, add_1_out_12, add_1_out_13, and_1_out, and_2_out, and_3_out, and_4_out,
       controlled_buffer_1_out, controlled_buffer_4_out, controlled_buffer_5_out, controlled_inverter_2_out,
       multiplexer_1_out, multiplexer_2_out, multiplexer_3_out, multiplexer_4_out, multiplexer_5_out,
       multiplexer_6_out, multiplexer_7_out, multiplexer_8_out, or_1_out, or_2_out, or_3_out, or_4_out,
       subs_1_out_10, subs_1_out_11, subs_1_out_12, subs_1_out_13, xor_1_out, xor_2_out, xor_3_out, xor_4_out;

  Multiplexer #(.select(2)) multiplexer_1 (.out(multiplexer_1_out), .sel(in_1), .en(in_7));  // open: in0, in1, in2, in3
  Multiplexer #(.select(2)) multiplexer_2 (.out(multiplexer_2_out), .sel(in_1), .en(in_7));  // open: in0, in1, in2, in3
  Multiplexer #(.select(2)) multiplexer_3 (.out(multiplexer_3_out), .sel(in_1), .en(in_7));  // open: in0, in1, in2, in3
  Multiplexer #(.select(2)) multiplexer_4 (.out(multiplexer_4_out), .sel(in_1), .en(in_7));  // open: in0, in1, in2, in3
  Multiplexer #(.select(2)) multiplexer_5 (.out(multiplexer_5_out), .sel(in_6), .en(in_7));  // open: in0, in1, in2, in3
  Multiplexer #(.select(2)) multiplexer_6 (.out(multiplexer_6_out), .sel(in_6), .en(in_7));  // open: in0, in1, in2, in3
  Multiplexer #(.select(2)) multiplexer_7 (.out(multiplexer_7_out), .sel(in_6), .en(in_7));  // open: in0, in1, in2, in3
  Multiplexer #(.select(2)) multiplexer_8 (.out(multiplexer_8_out), .sel(in_6), .en(in_7));  // open: in0, in1, in2, in3
  LED led_1 (.in(multiplexer_1_out));
  LED led_2 (.in(multiplexer_2_out));
  LED led_3 (.in(multiplexer_3_out));
  LED led_4 (.in(multiplexer_4_out));
  LED led_5 (.in(multiplexer_5_out));
  LED led_6 (.in(multiplexer_6_out));
  LED led_7 (.in(multiplexer_7_out));
  LED led_8 (.in(multiplexer_8_out));
  assign controlled_buffer_1_out = in_2 ? and_1_out : 1'bz;  // Controlled_Buffer controlled_buffer_1
  and and_1 (and_1_out, multiplexer_1_out, multiplexer_5_out);
  and and_2 (and_2_out, multiplexer_2_out, multiplexer_6_out);
  and and_3 (and_3_out, multiplexer_3_out, multiplexer_7_out);
  and and_4 (and_4_out, multiplexer_4_out, multiplexer_8_out);
  assign controlled_buffer_1_out = in_3 ? or_1_out : 1'bz;  // Controlled_Buffer controlled_buffer_2
  or or_1 (or_1_out, multiplexer_1_out, multiplexer_5_out);
  or or_2 (or_2_out, multiplexer_2_out, multiplexer_6_out);
  or or_3 (or_3_out, multiplexer_3_out, multiplexer_7_out);
  or or_4 (or_4_out, multiplexer_4_out, multiplexer_8_out);
  xor xor_1 (xor_1_out, multiplexer_1_out, multiplexer_5_out);
  xor xor_2 (xor_2_out, multiplexer_2_out, multiplexer_6_out);
  xor xor_3 (xor_3_out, multiplexer_3_out, multiplexer_7_out);
  xor xor_4 (xor_4_out, multiplexer_4_out, multiplexer_8_out);
  assign controlled_buffer_1_out = in_5 ? ~multiplexer_1_out : 1'bz;  // Controlled_Inverter controlled_inverter_1
  assign controlled_inverter_2_out = in_5 ? ~multiplexer_2_out : 1'bz;  // Controlled_Inverter controlled_inverter_2
  ADD add_1 (
    .A0(multiplexer_4_out), .A1(multiplexer_3_out), .A2(multiplexer_2_out), .A3(multiplexer_1_out),
    .B0(multiplexer_8_out), .B1(multiplexer_7_out), .B2(multiplexer_6_out), .B3(multiplexer_5_out),
    .in_1(in_8), .Overflow(Overflow), .out_10(add_1_out_10), .out_11(add_1_out_11), .out_12(add_1_out_12),
    .out_13(add_1_out_13));
  SUBS subs_1 (
    .A0(multiplexer_4_out), .A1(multiplexer_3_out), .A2(multiplexer_2_out), .A3(multiplexer_1_out),
    .B0(multiplexer_8_out), .B1(multiplexer_7_out), .B2(multiplexer_6_out), .B3(multiplexer_5_out),
    .in_2(in_10), .Overflow(Overflow_2), .out_10(subs_1_out_10), .out_11(subs_1_out_11),
    .out_12(subs_1_out_12), .out_13(subs_1_out_13));
  assign controlled_inverter_2_out = in_2 ? and_2_out : 1'bz;  // Controlled_Buffer controlled_buffer_3
  assign controlled_buffer_4_out = in_2 ? and_3_out : 1'bz;  // Controlled_Buffer controlled_buffer_4
  assign controlled_buffer_5_out = in_2 ? and_4_out : 1'bz;  // Controlled_Buffer controlled_buffer_5
  LED led_9 (.in(controlled_buffer_5_out));
  assign controlled_inverter_2_out = in_3 ? or_2_out : 1'bz;  // Controlled_Buffer controlled_buffer_6
  assign controlled_buffer_4_out = in_3 ? or_3_out : 1'bz;  // Controlled_Buffer controlled_buffer_7
  assign controlled_buffer_5_out = in_3 ? or_4_out : 1'bz;  // Controlled_Buffer controlled_buffer_8
  assign controlled_buffer_1_out = in_4 ? xor_1_out : 1'bz;  // Controlled_Buffer controlled_buffer_9
  assign controlled_inverter_2_out = in_4 ? xor_2_out : 1'bz;  // Controlled_Buffer controlled_buffer_10
  assign controlled_buffer_4_out = in_4 ? xor_3_out : 1'bz;  // Controlled_Buffer controlled_buffer_11
  assign controlled_buffer_5_out = in_4 ? xor_4_out : 1'bz;  // Controlled_Buffer controlled_buffer_12
  assign controlled_buffer_4_out = in_5 ? ~multiplexer_3_out : 1'bz;  // Controlled_Inverter controlled_inverter_3
  assign controlled_buffer_5_out = in_5 ? ~multiplexer_4_out : 1'bz;  // Controlled_Inverter controlled_inverter_4
  assign controlled_buffer_5_out = in_9 ? add_1_out_10 : 1'bz;  // Controlled_Buffer controlled_buffer_13
  assign controlled_buffer_4_out = in_9 ? add_1_out_11 : 1'bz;  // Controlled_Buffer controlled_buffer_14
  assign controlled_inverter_2_out = in_9 ? add_1_out_12 : 1'bz;  // Controlled_Buffer controlled_buffer_15
  assign controlled_buffer_1_out = in_9 ? add_1_out_13 : 1'bz;  // Controlled_Buffer controlled_buffer_16
  assign controlled_buffer_5_out = in_10 ? subs_1_out_10 : 1'bz;  // Controlled_Buffer controlled_buffer_17
  assign controlled_buffer_4_out = in_10 ? subs_1_out_11 : 1'bz;  // Controlled_Buffer controlled_buffer_18
  assign controlled_inverter_2_out = in_10 ? subs_1_out_12 : 1'bz;  // Controlled_Buffer controlled_buffer_19
  assign controlled_buffer_1_out = in_10 ? subs_1_out_13 : 1'bz;  // Controlled_Buffer controlled_buffer_20
endmodule

module ADD (
  input  in_1,
  input  A0,
  input  A1,
  input  A2,
  input  A3,
  input  B0,
  input  B1,
  input  B2,
  input  B3,
  output out_10,
  output out_11,
  output out_12,
  output out_13,
  output Overflow
);

  wire n1_bit_adder_1_c_out, n1_bit_adder_2_c_out, n1_bit_adder_3_c_out;

  _1_bit_adder u_1_bit_adder_1 (.A(A0), .B(B0), .C_in(in_1), .C_out(n1_bit_adder_1_c_out), .Sum(out_10));
  _1_bit_adder u_1_bit_adder_2 (
    .A(A1), .B(B1), .C_in(n1_bit_adder_1_c_out), .C_out(n1_bit_adder_2_c_out), .Sum(out_11));
  _1_bit_adder u_1_bit_adder_3 (
    .A(A2), .B(B2), .C_in(n1_bit_adder_2_c_out), .C_out(n1_bit_adder_3_c_out), .Sum(out_12));
  _1_bit_adder u_1_bit_adder_4 (.A(A3), .B(B3), .C_in(n1_bit_adder_3_c_out), .C_out(Overflow), .Sum(out_13));
endmodule

module _1_bit_adder (
  input  C_in,
  input  A,
  input  B,
  output Sum,
  output C_out
);

  wire and_1_out, and_2_out, and_3_out, xor_2_out;

  and and_1 (and_1_out, C_in, A);
  and and_2 (and_2_out, C_in, B);
  and and_3 (and_3_out, A, B);
  xor xor_1 (Sum, C_in, xor_2_out);
  xor xor_2 (xor_2_out, A, B);
  or or_1 (C_out, and_1_out, and_2_out, and_3_out);
endmodule

module SUBS (
  input  A0,
  input  in_2,
  input  A1,
  input  A2,
  input  A3,
  input  B0,
  input  B1,
  input  B2,
  input  B3,
  output out_10,
  output out_11,
  output out_12,
  output out_13,
  output Overflow
);

  wire n1_bit_adder_1_c_out, n1_bit_adder_2_c_out, n1_bit_adder_3_c_out, not_1_out, not_2_out, not_3_out,
       not_4_out;

  not not_1 (not_1_out, B2);
  not not_2 (not_2_out, B1);
  not not_3 (not_3_out, B0);
  not not_4 (not_4_out, B3);
  _1_bit_adder u_1_bit_adder_1 (.A(A0), .B(not_3_out), .C_in(in_2), .C_out(n1_bit_adder_1_c_out), .Sum(out_10));
  _1_bit_adder u_1_bit_adder_2 (
    .A(A1), .B(not_2_out), .C_in(n1_bit_adder_1_c_out), .C_out(n1_bit_adder_2_c_out), .Sum(out_11));
  _1_bit_adder u_1_bit_adder_3 (
    .A(A2), .B(not_1_out), .C_in(n1_bit_adder_2_c_out), .C_out(n1_bit_adder_3_c_out), .Sum(out_12));
  _1_bit_adder u_1_bit_adder_4 (.A(A3), .B(not_4_out), .C_in(n1_bit_adder_3_c_out), .C_out(Overflow), .Sum(out_13));
endmodule
